# Fritzing sketch arduinoProMini (saved by Fritzing 0.9.10b)
breadboards: 1

parts:
  Part3 = Arduino Pro Mini (5V)
  S1 = Momentary Switch [package=tactile-pth]
  LED1 = RGB LED (com. cathode, rbg) [package="5 mm [THT]"]
  R1 = Resistor [tolerance=±5% resistance=100 package="0805 [SMD]"]
  R2 = Resistor [tolerance=±5% resistance=100 package="0805 [SMD]"]
  R3 = Resistor [tolerance=±5% resistance=180 package="0805 [SMD]"]

nets:
  N1: Part3.VCC, LED1.common_cathode
  N2: Part3.GND, S1.3
  N3: Part3.D10, R2.Pin_1
  N4: Part3.D9, R1.Pin_1
  N5: Part3.D6, R3.Pin_1
  N6: Part3.D2, S1.1
  N7: LED1.red_anode, R3.Pin_0
  N8: LED1.blue_anode, R2.Pin_0
  N9: LED1.green_anode, R1.Pin_0
